# Fritzing sketch Arduino_Fan_using potentiometer (saved by Fritzing 1.0.4)
breadboards: 2

parts:
  Part1 = Arduino Uno (Rev3) - ICSP
  IC1 = L293D [package=THT]
  Part2 = Arduino Uno (Rev3) - ICSP
  R1 = Rotary Potentiometer (Large) [maximum_resistance=10kΩ knob_status=50% power=0.5W package=THT]
  LED1 = smd LED [color="Red (633nm)" package="0805 [SMD]"]
  LED3 = smd LED [color="Green (570nm)" package="0805 [SMD]"]
  LED4 = smd LED [color="Blue (525nm)" package="0805 [SMD]"]
  R2 = Resistor [tolerance=±5% resistance=220 package="2010 [SMD]"]
  R3 = Resistor [tolerance=±5% resistance=220 package="2010 [SMD]"]
  R4 = Resistor [tolerance=±5% resistance=220 package="2010 [SMD]"]
  Q1 = NPN-Transistor [package="TO92 [THT]"]
  R5 = Resistor [tolerance=±5% resistance=1k package="2010 [SMD]"]
  M1 = DC Motor [voltage_(max)=6V voltage_(min)=3V]

nets:
  N1: Part1.A0, R1.wiper
  N2: Part1.D8, IC1.In_1
  N3: Part1.D9_PWM, IC1.Enable_1
  N4: Part1.D2, LED1.cathode
  N5: Part1.D3_PWM, LED3.cathode
  N6: Part1.D4, LED4.cathode
  N7: Part1.D7, IC1.In_2
  N8: IC1.Out_1_(_Controlled_by_Enable_1_), Q1.B, R5.Pin_0, R5.Pin_1, M1.pin_2
  N9: IC1.0V, Part2.GND, R1.leg2, R2.Pin_1, R3.Pin_1, R4.Pin_1, Q1.C
  N10: IC1.+Vmotor, Part2.VIN
  N11: IC1.Enable_2, Part2.D6_PWM
  N12: IC1.+V, R1.leg1
  N13: LED1.anode, R4.Pin_0
  N14: LED3.anode, R3.Pin_0
  N15: LED4.anode, R2.Pin_0
  N16: Q1.E, M1.pin_1
